# Fritzing sketch PCB (saved by Fritzing 0.9.2b)
circuit board: 5.62589cm x 4.42834cm
breadboards: 1

parts:
  J5 = shrouded pin header, 14 pins [form="♂ (shrouded male)"]
  J1 = male pin header, 5 pins [form="♂ (male)"]
  J3 = male pin header, 3 pins [form="♂ (male)"]
  J2 = male pin header, 2 pins [form="♂ (male)"]
  Nano1 = Arduino Nano v2.3
  R1 = Trimmer Potentiometer [maximum_resistance=10kΩ package=THT]
  J4 = screw terminal, 2 pins

nets:
  GND: J5.pin1, J5.pin3, J1.pin2, J3.pin2, J2.pin1, Nano1.GND, R1.leg1, J4.pin2
  N1: J5.pin2, R1.wiper
  N2: J5.pin6, Nano1.D5
  N3: J5.pin7, Nano1.D3
  N4: J5.pin8, Nano1.D2
  N5: J5.pin9, Nano1.D4
  N6: J5.pin12, Nano1.D6
  N7: J5.pin13, Nano1.D7
  5V: J5.pin14, J1.pin1, J3.pin3, Nano1.+5V, R1.leg2, J4.pin1
  N8: J1.pin3, Nano1.D12
  N9: J1.pin4, Nano1.D11
  N10: J1.pin5, Nano1.D10
  N11: J3.pin1, Nano1.D8
  N12: J2.pin2, Nano1.D9

notes:
  Gärbox v0.2
